# Fritzing sketch Motor diagram (saved by Fritzing 0.9.3b)

parts:
  Part1 = Arduino Uno (Rev3) - ICSP  # not connected
  MD03A1 = Dual VNH2SP30 Motor Driver [part_number=MD03A]
  M1 = DC Motor
  M2 = DC Motor
  JP1 = Header 4 [package=1x04-smd]  # not connected
  JP2 = Header 4 [package=1x04-smd]  # not connected

nets:
  N1: MD03A1.OUT_1A, M1.pin_1
  N2: MD03A1.OUT_1B, M2.pin_1
  N3: MD03A1.OUT_2A, M1.pin_2
  N4: MD03A1.OUT_2B, M2.pin_2

notes:
  Motor1
  Motor2
  Encoder Motor1
  Encoder Motor2
